// Logisim project Something Interesting.circ as structural Verilog: 7 circuits, main circuit main
module main (
  input  in_1
);

  wire CLK, RAWCLK, Reset;
  wire [3:0] BAD, GOOD, MISS, score_1_out_5, score_1_out_6, score_1_out_7, score_2_out_5, score_2_out_6,
       score_2_out_7, score_3_out_5, score_3_out_6, score_3_out_7;
  wire [6:0] Input;
  wire [7:0] Correct, keyboardreader_1_out_2, readbuffer_1_output;
  wire [15:0] datatoscreen_1_out_5, datatoscreen_1_out_6, datatoscreen_1_out_7, datatoscreen_1_out_8,
       datatoscreen_1_out_9, datatoscreen_1_out_10, datatoscreen_1_out_11, datatoscreen_1_out_12;

  Clock clock_1 (.out(RAWCLK));
  Button button_1 (.out(Reset));
  DataToScreen datatoscreen_1 (
    .CLK(CLK), .RST(Reset), .out_5(datatoscreen_1_out_5), .out_6(datatoscreen_1_out_6),
    .out_7(datatoscreen_1_out_7), .out_8(datatoscreen_1_out_8), .out_9(datatoscreen_1_out_9),
    .out_10(datatoscreen_1_out_10), .out_11(datatoscreen_1_out_11), .out_12(datatoscreen_1_out_12),
    .CRT(Correct), .RAND(in_1));
  DotMatrix #(.matrixcols(16), .matrixrows(16)) dotmatrix_1 (
    .col0(datatoscreen_1_out_5), .col1(datatoscreen_1_out_5), .col2(datatoscreen_1_out_6),
    .col3(datatoscreen_1_out_6), .col4(datatoscreen_1_out_7), .col5(datatoscreen_1_out_7),
    .col6(datatoscreen_1_out_8), .col7(datatoscreen_1_out_8), .col8(datatoscreen_1_out_9),
    .col9(datatoscreen_1_out_9), .col10(datatoscreen_1_out_10), .col11(datatoscreen_1_out_10),
    .col12(datatoscreen_1_out_11), .col13(datatoscreen_1_out_11), .col14(datatoscreen_1_out_12),
    .col15(datatoscreen_1_out_12));
  Keyboard #(.buflen(1)) keyboard_1 (.clk(RAWCLK), .data(Input));  // open: re, clr, avail
  KeyboardReader keyboardreader_1 (.Input(Input), .out_2(keyboardreader_1_out_2));
  ReadBuffer readbuffer_1 (.INPUT(keyboardreader_1_out_2), .CLK(RAWCLK), .CLR(CLK), .OUTPUT(readbuffer_1_output));
  Checker checker_1 (.INPUT(readbuffer_1_output), .CORRECT(Correct), .GOOD(GOOD), .MISS(MISS), .BAD(BAD));
  Hex_Digit_Display hex_digit_display_1 (.value(score_1_out_7));  // open: dp
  Score score_1 (
    .ADD(GOOD), .CLK(CLK), .out_5(score_1_out_5), .out_6(score_1_out_6), .out_7(score_1_out_7), .RST(Reset),
    .RAWCLK(RAWCLK));
  Hex_Digit_Display hex_digit_display_2 (.value(score_1_out_6));  // open: dp
  Score score_2 (
    .ADD(MISS), .CLK(CLK), .out_5(score_2_out_5), .out_6(score_2_out_6), .out_7(score_2_out_7), .RST(Reset),
    .RAWCLK(RAWCLK));
  Hex_Digit_Display hex_digit_display_3 (.value(score_2_out_7));  // open: dp
  Hex_Digit_Display hex_digit_display_4 (.value(score_1_out_5));  // open: dp
  ReduceFrequency reducefrequency_1 (.OUTPUT(CLK), .CLK(RAWCLK));
  Hex_Digit_Display hex_digit_display_5 (.value(score_2_out_6));  // open: dp
  Hex_Digit_Display hex_digit_display_6 (.value(score_2_out_5));  // open: dp
  Hex_Digit_Display hex_digit_display_7 (.value(score_3_out_7));  // open: dp
  Score score_3 (
    .ADD(BAD), .CLK(CLK), .out_5(score_3_out_5), .out_6(score_3_out_6), .out_7(score_3_out_7), .RST(Reset),
    .RAWCLK(RAWCLK));
  Hex_Digit_Display hex_digit_display_8 (.value(score_3_out_6));  // open: dp
  Hex_Digit_Display hex_digit_display_9 (.value(score_3_out_5));  // open: dp

  // Other names for the same wires on the sheet: Random = in_1

  // Notes on the sheet:
  //   A    S    D    F    H    J    K    L
  //   Set Tick Frequency to 1KHz
endmodule

module KeyboardReader (
  input  [6:0] Input,
  output [7:0] out_2
);

  Comparator #(.width(7), .mode("unsigned")) comparator_1 (.a(Input), .b(7'b1100001), .eq(out_2[0]));  // open: gt, lt
  Comparator #(.width(7), .mode("unsigned")) comparator_2 (.a(Input), .b(7'b1110011), .eq(out_2[1]));  // open: gt, lt
  Comparator #(.width(7), .mode("unsigned")) comparator_3 (.a(Input), .b(7'b1100100), .eq(out_2[2]));  // open: gt, lt
  Comparator #(.width(7), .mode("unsigned")) comparator_4 (.a(Input), .b(7'b1100110), .eq(out_2[3]));  // open: gt, lt
  Comparator #(.width(7), .mode("unsigned")) comparator_5 (.a(Input), .b(7'b1100111));  // open: gt, eq, lt
  Comparator #(.width(7), .mode("unsigned")) comparator_6 (.a(Input), .b(7'b1101000), .eq(out_2[4]));  // open: gt, lt
  Comparator #(.width(7), .mode("unsigned")) comparator_7 (.a(Input), .b(7'b1101010), .eq(out_2[5]));  // open: gt, lt
  Comparator #(.width(7), .mode("unsigned")) comparator_8 (.a(Input), .b(7'b1101011), .eq(out_2[6]));  // open: gt, lt
  Comparator #(.width(7), .mode("unsigned")) comparator_9 (.a(Input), .b(7'b1101100), .eq(out_2[7]));  // open: gt, lt
endmodule

module DataToScreen (
  input  CLK,
  input  RST,
  input  RAND,
  output [7:0] CRT,
  output [15:0] out_5,
  output [15:0] out_6,
  output [15:0] out_7,
  output [15:0] out_8,
  output [15:0] out_9,
  output [15:0] out_10,
  output [15:0] out_11,
  output [15:0] out_12
);

  wire [2:0] random_1_out;
  wire [7:0] decoder_1_out0, multiplexer_1_out, rom_1_data;
  wire [23:0] counter_1_q;

  Counter #(.width(24), .max('hffffff)) counter_1 (
    .Q(counter_1_q), .clk(CLK), .clr(RST));  // open: load, D, count, carry
  ROM #(.addrWidth(24)) rom_1 (.addr(counter_1_q), .data(rom_1_data));  // open: sel
  Random #(.width(3)) random_1 (.clk(CLK), .next(RAND), .out(random_1_out));  // open: clr
  Decoder #(.select(3)) decoder_1 (
    .out0(decoder_1_out0[0]), .out1(decoder_1_out0[1]), .out2(decoder_1_out0[2]), .out3(decoder_1_out0[3]),
    .out4(decoder_1_out0[4]), .out5(decoder_1_out0[5]), .out6(decoder_1_out0[6]), .out7(decoder_1_out0[7]),
    .sel(random_1_out), .en(RAND));
  Multiplexer #(.width(8)) multiplexer_1 (
    .in0(rom_1_data), .in1(decoder_1_out0), .out(multiplexer_1_out), .sel(RAND));  // open: en
  Shift_Register #(.length(16)) shift_register_1 (
    .shift(1'b1), .in(multiplexer_1_out[0]), .clk(CLK), .out(CRT[0]), .q0(out_5[15]), .q1(out_5[14]),
    .q2(out_5[13]), .q3(out_5[12]), .q4(out_5[11]), .q5(out_5[10]), .q6(out_5[9]), .q7(out_5[8]),
    .q8(out_5[7]), .q9(out_5[6]), .q10(out_5[5]), .q11(out_5[4]), .q12(out_5[3]), .q13(out_5[2]),
    .q14(out_5[1]), .q15(out_5[0]));  // open: load, clr, d0, d1, d2, d3, d4, d5, d6, d7, d8, d9, d10, d11, d12, d13, d14, d15
  Shift_Register #(.length(16)) shift_register_2 (
    .shift(1'b1), .in(multiplexer_1_out[1]), .clk(CLK), .out(CRT[1]), .q0(out_6[15]), .q1(out_6[14]),
    .q2(out_6[13]), .q3(out_6[12]), .q4(out_6[11]), .q5(out_6[10]), .q6(out_6[9]), .q7(out_6[8]),
    .q8(out_6[7]), .q9(out_6[6]), .q10(out_6[5]), .q11(out_6[4]), .q12(out_6[3]), .q13(out_6[2]),
    .q14(out_6[1]), .q15(out_6[0]));  // open: load, clr, d0, d1, d2, d3, d4, d5, d6, d7, d8, d9, d10, d11, d12, d13, d14, d15
  Shift_Register #(.length(16)) shift_register_3 (
    .shift(1'b1), .in(multiplexer_1_out[2]), .clk(CLK), .out(CRT[2]), .q0(out_7[15]), .q1(out_7[14]),
    .q2(out_7[13]), .q3(out_7[12]), .q4(out_7[11]), .q5(out_7[10]), .q6(out_7[9]), .q7(out_7[8]),
    .q8(out_7[7]), .q9(out_7[6]), .q10(out_7[5]), .q11(out_7[4]), .q12(out_7[3]), .q13(out_7[2]),
    .q14(out_7[1]), .q15(out_7[0]));  // open: load, clr, d0, d1, d2, d3, d4, d5, d6, d7, d8, d9, d10, d11, d12, d13, d14, d15
  Shift_Register #(.length(16)) shift_register_4 (
    .shift(1'b1), .in(multiplexer_1_out[3]), .clk(CLK), .out(CRT[3]), .q0(out_8[15]), .q1(out_8[14]),
    .q2(out_8[13]), .q3(out_8[12]), .q4(out_8[11]), .q5(out_8[10]), .q6(out_8[9]), .q7(out_8[8]),
    .q8(out_8[7]), .q9(out_8[6]), .q10(out_8[5]), .q11(out_8[4]), .q12(out_8[3]), .q13(out_8[2]),
    .q14(out_8[1]), .q15(out_8[0]));  // open: load, clr, d0, d1, d2, d3, d4, d5, d6, d7, d8, d9, d10, d11, d12, d13, d14, d15
  Shift_Register #(.length(16)) shift_register_5 (
    .shift(1'b1), .in(multiplexer_1_out[4]), .clk(CLK), .out(CRT[4]), .q0(out_9[15]), .q1(out_9[14]),
    .q2(out_9[13]), .q3(out_9[12]), .q4(out_9[11]), .q5(out_9[10]), .q6(out_9[9]), .q7(out_9[8]),
    .q8(out_9[7]), .q9(out_9[6]), .q10(out_9[5]), .q11(out_9[4]), .q12(out_9[3]), .q13(out_9[2]),
    .q14(out_9[1]), .q15(out_9[0]));  // open: load, clr, d0, d1, d2, d3, d4, d5, d6, d7, d8, d9, d10, d11, d12, d13, d14, d15
  Shift_Register #(.length(16)) shift_register_6 (
    .shift(1'b1), .in(multiplexer_1_out[5]), .clk(CLK), .out(CRT[5]), .q0(out_10[15]), .q1(out_10[14]),
    .q2(out_10[13]), .q3(out_10[12]), .q4(out_10[11]), .q5(out_10[10]), .q6(out_10[9]), .q7(out_10[8]),
    .q8(out_10[7]), .q9(out_10[6]), .q10(out_10[5]), .q11(out_10[4]), .q12(out_10[3]), .q13(out_10[2]),
    .q14(out_10[1]), .q15(out_10[0]));  // open: load, clr, d0, d1, d2, d3, d4, d5, d6, d7, d8, d9, d10, d11, d12, d13, d14, d15
  Shift_Register #(.length(16)) shift_register_7 (
    .shift(1'b1), .in(multiplexer_1_out[6]), .clk(CLK), .out(CRT[6]), .q0(out_11[15]), .q1(out_11[14]),
    .q2(out_11[13]), .q3(out_11[12]), .q4(out_11[11]), .q5(out_11[10]), .q6(out_11[9]), .q7(out_11[8]),
    .q8(out_11[7]), .q9(out_11[6]), .q10(out_11[5]), .q11(out_11[4]), .q12(out_11[3]), .q13(out_11[2]),
    .q14(out_11[1]), .q15(out_11[0]));  // open: load, clr, d0, d1, d2, d3, d4, d5, d6, d7, d8, d9, d10, d11, d12, d13, d14, d15
  Shift_Register #(.length(16)) shift_register_8 (
    .shift(1'b1), .in(multiplexer_1_out[7]), .clk(CLK), .out(CRT[7]), .q0(out_12[15]), .q1(out_12[14]),
    .q2(out_12[13]), .q3(out_12[12]), .q4(out_12[11]), .q5(out_12[10]), .q6(out_12[9]), .q7(out_12[8]),
    .q8(out_12[7]), .q9(out_12[6]), .q10(out_12[5]), .q11(out_12[4]), .q12(out_12[3]), .q13(out_12[2]),
    .q14(out_12[1]), .q15(out_12[0]));  // open: load, clr, d0, d1, d2, d3, d4, d5, d6, d7, d8, d9, d10, d11, d12, d13, d14, d15

  // Notes on the sheet:
  //   contents of rom_1 (hex, n*v repeats v):
  //   1 2 4 8 10 20 40 80 80 40 20 10 8 4 2 1 1 3 6 c 18 30 60 c0 c0 60 30 18 c 6 3 1 81 42 24 18 81 18 42
  //   24 24 18 81 42 42 18 81 24
endmodule

module Score (
  input  RST,
  input  [3:0] ADD,
  input  CLK,
  input  RAWCLK,
  output [3:0] out_5,
  output [3:0] out_6,
  output [3:0] out_7
);

  wire and_1_out, and_2_out, comparator_1_eq, counter_1_carry, counter_3_carry, not_1_out, not_2_out;
  wire [3:0] counter_2_q, register_1_q;

  Register #(.width(4)) register_1 (.D(ADD), .en(1'b1), .Q(register_1_q), .clk(RAWCLK));  // open: clr
  not not_1 (not_1_out, CLK);
  Counter #(.width(4), .max('h9)) counter_1 (
    .count(not_2_out), .Q(out_5), .carry(counter_1_carry), .clk(RAWCLK), .clr(RST));  // open: load, D
  Counter #(.width(4), .max('hf), .ongoal("stay")) counter_2 (
    .load(1'b1), .D(register_1_q), .count(not_1_out), .Q(counter_2_q), .clk(RAWCLK));  // open: carry, clr
  and and_1 (and_1_out, not_2_out, counter_1_carry);
  not not_2 (not_2_out, comparator_1_eq);
  Comparator #(.width(4)) comparator_1 (.a(4'b0000), .b(counter_2_q), .eq(comparator_1_eq));  // open: gt, lt
  Counter #(.width(4), .max('h9)) counter_3 (
    .count(and_1_out), .Q(out_6), .carry(counter_3_carry), .clk(RAWCLK), .clr(RST));  // open: load, D
  and and_2 (and_2_out, not_2_out, counter_3_carry);
  Counter #(.width(4), .max('h9)) counter_4 (
    .count(and_2_out), .Q(out_7), .clk(RAWCLK), .clr(RST));  // open: load, D, carry
endmodule

module ReadBuffer (
  input  [7:0] INPUT,
  input  CLK,
  input  CLR,
  output [7:0] OUTPUT
);

  wire [7:0] or_1_out;

  assign or_1_out = OUTPUT | INPUT;  // OR_Gate or_1, 8 bits wide
  Register register_1 (.D(or_1_out), .Q(OUTPUT), .clk(CLK), .clr(CLR));  // open: en
endmodule

module ReduceFrequency (
  input  CLK,
  output OUTPUT
);

  Counter #(.max('hcf)) counter_1 (.count(1'b1), .carry(OUTPUT), .clk(CLK));  // open: load, D, Q, clr
endmodule

module Checker (
  input  [7:0] INPUT,
  input  [7:0] CORRECT,
  output [3:0] GOOD,
  output [3:0] MISS,
  output [3:0] BAD
);

  wire [7:0] and_1_out, and_2_out, and_3_out, not_1_out, not_2_out;

  assign not_1_out = ~INPUT;  // NOT_Gate not_1, 8 bits wide
  assign not_2_out = ~CORRECT;  // NOT_Gate not_2, 8 bits wide
  assign and_1_out = INPUT & CORRECT;  // AND_Gate and_1, 8 bits wide
  assign and_2_out = not_1_out & CORRECT;  // AND_Gate and_2, 8 bits wide
  assign and_3_out = INPUT & not_2_out;  // AND_Gate and_3, 8 bits wide
  BitAdder bitadder_1 (.in0(and_1_out), .out(GOOD));
  BitAdder bitadder_2 (.in0(and_2_out), .out(MISS));
  BitAdder bitadder_3 (.in0(and_3_out), .out(BAD));
endmodule
